# Fritzing sketch schematic (saved by Fritzing 0.8.7b)
breadboards: 1

parts:
  Part1 = Arduino Uno (Rev3)  # not connected
  Part2 = Arduino Ethernet Shield (Rev3)
  Q1 = NPN-Transistor [package="TO92 [THT]"]
  U4 = RELAY-SOLIDSTATE [package=relay-s108t02]
  LED1 = LED - 5mm [color="Red (633nm)" package="5 mm [THT]"]

nets:
  N1: Part2.PWM_D9, LED1.cathode
  N2: Part2.5V, Q1.E
  N3: Part2.GND, U4.-
  N4: Q1.B, LED1.anode
  N5: Q1.C, U4.+

notes:
  Door buzzer
